// Logisim project Count8.circ as structural Verilog: 1 circuit, main circuit main
module main (
  input  reset,
  input  clock,
  input  set,
  output [7:0] out_4
);

  wire and_1_out, and_2_out, and_3_out, and_4_out, and_5_out, and_6_out;

  J_K_Flip_Flop j_k_ff_1 (.J(1'b1), .clk(clock), .K(1'b1), .Q(out_4[0]), .preset(reset), .reset(set));  // open: Qn
  J_K_Flip_Flop j_k_ff_2 (
    .J(out_4[0]), .clk(clock), .K(out_4[0]), .Q(out_4[1]), .preset(reset), .reset(set));  // open: Qn
  and and_1 (and_1_out, out_4[0], out_4[1]);
  J_K_Flip_Flop j_k_ff_3 (
    .J(and_1_out), .clk(clock), .K(and_1_out), .Q(out_4[2]), .preset(reset), .reset(set));  // open: Qn
  and and_2 (and_2_out, and_1_out, out_4[2]);
  J_K_Flip_Flop j_k_ff_4 (
    .J(and_2_out), .clk(clock), .K(and_2_out), .Q(out_4[3]), .preset(reset), .reset(set));  // open: Qn
  and and_3 (and_3_out, and_2_out, out_4[3]);
  J_K_Flip_Flop j_k_ff_5 (
    .J(and_3_out), .clk(clock), .K(and_3_out), .Q(out_4[4]), .preset(reset), .reset(set));  // open: Qn
  and and_4 (and_4_out, and_3_out, out_4[4]);
  J_K_Flip_Flop j_k_ff_6 (
    .J(and_4_out), .clk(clock), .K(and_4_out), .Q(out_4[5]), .preset(reset), .reset(set));  // open: Qn
  and and_5 (and_5_out, and_4_out, out_4[5]);
  J_K_Flip_Flop j_k_ff_7 (
    .J(and_5_out), .clk(clock), .K(and_5_out), .Q(out_4[6]), .preset(reset), .reset(set));  // open: Qn
  and and_6 (and_6_out, and_5_out, out_4[6]);
  J_K_Flip_Flop j_k_ff_8 (
    .J(and_6_out), .clk(clock), .K(and_6_out), .Q(out_4[7]), .preset(reset), .reset(set));  // open: Qn
endmodule
