// Logisim project ROM_spatti.circ as structural Verilog: 1 circuit, main circuit main
module main (
  input  [7:0] busAddr8,
  input  CLK,
  output [15:0] busData16
);

  wire [15:0] ROM_CPU_data;

  ROM #(.dataWidth(16), .Select("low")) ROM_CPU (.addr(busAddr8), .data(ROM_CPU_data));
  Register #(.width(16), .Select("low")) Reg16 (.D(ROM_CPU_data), .Q(busData16), .clk(CLK));  // open: en, clr

  // Notes on the sheet:
  //   contents of ROM_CPU (hex, n*v repeats v):
  //   6005 9101 6202 6304 c08 0 0 0 400 6001 9001 9002 6302 6102 9302 6200 6001 800
endmodule
