// Logisim project ULA4.circ as structural Verilog: 1 circuit, main circuit main
module main (
  input  [3:0] in_1,
  input  [3:0] in_2,
  input  [1:0] in_3,
  output [3:0] out_4,
  output [3:0] out_5,
  output [3:0] out_6,
  output [3:0] out_7,
  output [3:0] out_8
);

  Adder #(.width(4)) adder_1 (.a(in_1), .b(in_2), .out(out_4));  // open: cin, cout
  Multiplier #(.width(4)) multiplier_1 (.a(in_1), .b(4'b0010), .out(out_5));  // open: cin, cout
  Subtractor #(.width(4)) subtractor_1 (.a(in_1), .b(in_2), .out(out_6));  // open: bin, bout
  Divider #(.width(4)) divider_1 (.a(in_1), .b(4'b0010), .out(out_8));  // open: upper, rem
  Multiplexer #(.select(2), .width(4), .enable("false")) multiplexer_1 (
    .in0(out_4), .in1(out_5), .in2(out_6), .in3(out_8), .out(out_7), .sel(in_3));
endmodule
