// Logisim project contador.circ as structural Verilog: 1 circuit, main circuit main
module main (
  input  reset,
  input  clock,
  input  set,
  output q1,
  output q2,
  output q4,
  output q0
);

  wire t_ff_1_q, t_ff_2_q, t_ff_3_q;

  T_Flip_Flop t_ff_1 (.clk(clock), .T(1'b1), .Q(t_ff_1_q), .Qn(q0), .preset(reset), .reset(set));
  T_Flip_Flop t_ff_2 (.clk(t_ff_1_q), .T(1'b1), .Q(t_ff_2_q), .Qn(q1), .preset(reset), .reset(set));
  T_Flip_Flop t_ff_3 (.clk(t_ff_2_q), .T(1'b1), .Q(t_ff_3_q), .Qn(q2), .preset(reset), .reset(set));
  T_Flip_Flop t_ff_4 (.clk(t_ff_3_q), .T(1'b1), .Qn(q4), .preset(reset), .reset(set));  // open: Q
endmodule
