// Logisim project cpu.circ as structural Verilog: 6 circuits, main circuit DE0cv
module contador_8bits (
  input  [3:0] data,
  input  jump,
  input  clock,
  input  reset,
  output [7:0] out_5
);

  wire and_1_out, and_2_out, and_3_out, and_4_out, and_5_out, and_6_out, and_7_out, and_8_out, and_9_out,
       and_10_out, and_11_out, and_12_out, and_13_out, and_14_out, and_15_out, and_16_out, and_17_out,
       and_18_out, and_19_out, and_20_out, and_21_out, and_22_out, not_1_out, not_2_out, not_3_out,
       not_4_out, not_5_out, not_6_out, not_7_out, not_8_out, or_1_out, or_2_out, or_3_out, or_4_out,
       or_5_out, or_6_out, or_7_out, or_8_out;

  and and_1 (and_1_out, jump, data[0]);
  not not_1 (not_1_out, data[0]);
  and and_2 (and_2_out, not_1_out, jump);
  T_Flip_Flop t_ff_1 (.clk(clock), .T(1'b1), .Q(out_5[0]), .preset(and_1_out), .reset(or_1_out));  // open: Qn
  or or_1 (or_1_out, and_2_out, reset);
  not not_2 (not_2_out, data[1]);
  and and_3 (and_3_out, not_2_out, jump);
  or or_2 (or_2_out, and_3_out, reset);
  and and_4 (and_4_out, data[1], jump);
  T_Flip_Flop t_ff_2 (.clk(clock), .T(out_5[0]), .Q(out_5[1]), .preset(and_4_out), .reset(or_2_out));  // open: Qn
  not not_3 (not_3_out, data[2]);
  and and_5 (and_5_out, data[2], jump);
  and and_6 (and_6_out, out_5[1], out_5[0]);
  and and_7 (and_7_out, not_3_out, jump);
  or or_3 (or_3_out, and_7_out, reset);
  T_Flip_Flop t_ff_3 (.clk(clock), .T(and_6_out), .Q(out_5[2]), .preset(and_5_out), .reset(or_3_out));  // open: Qn
  and and_8 (and_8_out, out_5[2], and_6_out);
  not not_4 (not_4_out, data[3]);
  and and_9 (and_9_out, not_4_out, jump);
  and and_10 (and_10_out, data[3], jump);
  T_Flip_Flop t_ff_4 (.clk(clock), .T(and_8_out), .Q(out_5[3]), .preset(and_10_out), .reset(or_4_out));  // open: Qn
  or or_4 (or_4_out, and_9_out, reset);
  not not_5 (not_5_out, 1'b0);
  and and_11 (and_11_out, 1'b0, jump);
  and and_12 (and_12_out, out_5[3], and_8_out);
  and and_13 (and_13_out, not_5_out, jump);
  or or_5 (or_5_out, and_13_out, reset);
  T_Flip_Flop t_ff_5 (.clk(clock), .T(and_12_out), .Q(out_5[4]), .preset(and_11_out), .reset(or_5_out));  // open: Qn
  and and_14 (and_14_out, out_5[4], and_12_out);
  not not_6 (not_6_out, 1'b0);
  and and_15 (and_15_out, not_6_out, jump);
  and and_16 (and_16_out, 1'b0, jump);
  T_Flip_Flop t_ff_6 (.clk(clock), .T(and_14_out), .Q(out_5[5]), .preset(and_16_out), .reset(or_6_out));  // open: Qn
  or or_6 (or_6_out, and_15_out, reset);
  and and_17 (and_17_out, out_5[5], and_14_out);
  not not_7 (not_7_out, 1'b0);
  and and_18 (and_18_out, not_7_out, jump);
  and and_19 (and_19_out, 1'b0, jump);
  T_Flip_Flop t_ff_7 (.clk(clock), .T(and_17_out), .Q(out_5[6]), .preset(and_19_out), .reset(or_7_out));  // open: Qn
  or or_7 (or_7_out, and_18_out, reset);
  not not_8 (not_8_out, 1'b0);
  and and_20 (and_20_out, 1'b0, jump);
  and and_21 (and_21_out, out_5[6], and_17_out);
  and and_22 (and_22_out, not_8_out, jump);
  or or_8 (or_8_out, and_22_out, reset);
  T_Flip_Flop t_ff_8 (.clk(clock), .T(and_21_out), .Q(out_5[7]), .preset(and_20_out), .reset(or_8_out));  // open: Qn
endmodule

module registrador_4bits (
  input  clock,
  input  preset,
  input  clear,
  input  [3:0] \input ,
  output [3:0] out_5
);

  wire d_ff_2_qn;

  D_Flip_Flop #(.Pre_Clr_Positions("LEGACY")) d_ff_1 (
    .clk(clock), .D(\input [0]), .Q(out_5[0]), .preset(preset), .reset(clear));  // open: Qn
  D_Flip_Flop d_ff_2 (.clk(clock), .D(\input [1]), .Q(out_5[1]), .Qn(d_ff_2_qn), .preset(preset), .reset(clear));
  D_Flip_Flop d_ff_3 (.clk(clock), .D(\input [2]), .Q(out_5[2]), .preset(preset), .reset(clear));  // open: Qn
  D_Flip_Flop d_ff_4 (.clk(clock), .D(\input [3]), .Q(out_5[3]), .reset(clear));  // open: Qn, preset
endmodule

module ULA (
  input  [1:0] OP,
  input  [3:0] A,
  input  [3:0] B,
  output [3:0] \SAÍDA 
);

  wire [3:0] adder_1_out, divider_1_out, multiplier_1_out, subtractor_1_out;

  Adder #(.width(4)) adder_1 (.a(A), .b(B), .out(adder_1_out));  // open: cin, cout
  Multiplier #(.width(4)) multiplier_1 (.a(A), .b(4'b0010), .out(multiplier_1_out));  // open: cin, cout
  Subtractor #(.width(4)) subtractor_1 (.a(A), .b(B), .out(subtractor_1_out));  // open: bin, bout
  Divider #(.width(4)) divider_1 (.a(A), .b(4'b0010), .out(divider_1_out));  // open: upper, rem
  Multiplexer #(.select(2), .width(4), .enable("false")) multiplexer_1 (
    .in0(adder_1_out), .in1(multiplier_1_out), .in2(subtractor_1_out), .in3(divider_1_out), .out(\SAÍDA ),
    .sel(OP));
endmodule

module DE0cv (
  output [3:0] out_1
);

  wire and_1_out, CLK_R1, CLK_R2, CLR, CLR_REG, JMP, K0, K1, K2, K3, L0, L1, L2, L3, L4, L5, L6, L7, L8, L9,
       not_1_out, not_2_out, S0, S1, S2, S3, S4, S5, S6, S6_p1, S7, S8, S9;
  wire [1:0] OP_ULA;
  wire [3:0] HEX0, HEX1, HEX2, HEX3, HEX4, HEX5, OPERANDO, OUT_ULA, ULA_IN_A, ULA_IN_B;

  Hex_Digit_Display hex_digit_display_1 (.value(HEX5));  // open: dp
  LED u_L8 (.in(L8));
  LED u_L9 (.in(L9));
  // DipSwitch #(.NSwitches(1)) S9: pin names not known; wires that end beside it: S9
  // DipSwitch #(.NSwitches(1)) S8: pin names not known; wires that end beside it: S8
  Hex_Digit_Display hex_digit_display_2 (.value(HEX3));  // open: dp
  Hex_Digit_Display hex_digit_display_3 (.value(HEX4));  // open: dp
  LED u_L7 (.in(L7));
  LED u_L6 (.in(L6));
  LED u_L5 (.in(L5));
  // DipSwitch #(.NSwitches(1)) S5: pin names not known; wires that end beside it: S5
  // DipSwitch #(.NSwitches(1)) S7: pin names not known; wires that end beside it: S7
  // DipSwitch #(.NSwitches(1)) S6: pin names not known; wires that end beside it: S6_p1, S6
  ULA ula_1 (.A(ULA_IN_B), .B(ULA_IN_A), .OP(OP_ULA), .\SAÍDA (OUT_ULA));
  registrador_4bits registrador_4bits_1 (
    .clock(CLK_R1), .preset(S6_p1), .clear(CLR_REG), .\input (OUT_ULA), .out_5(HEX1));
  registrador_4bits registrador_4bits_2 (
    .clock(CLK_R2), .clear(CLR_REG), .\input (OUT_ULA), .out_5(HEX0));  // open: preset
  Hex_Digit_Display hex_digit_display_4 (.value(HEX2));  // open: dp
  LED u_L4 (.in(L4));
  LED u_L3 (.in(L3));
  // DipSwitch #(.NSwitches(1)) S3: pin names not known; wires that end beside it: S3
  // DipSwitch #(.NSwitches(1)) S2: pin names not known; wires that end beside it: S2
  // DipSwitch #(.NSwitches(1)) S4: pin names not known; wires that end beside it: S4
  Hex_Digit_Display hex_digit_display_5 (.value(HEX1));  // open: dp
  Hex_Digit_Display hex_digit_display_6 (.value(HEX0));  // open: dp
  LED u_L0 (.in(L0));
  LED u_L1 (.in(L1));
  LED u_L2 (.in(L2));
  // DipSwitch #(.NSwitches(1)) S0: pin names not known; wires that end beside it: S0
  // DipSwitch #(.NSwitches(1)) S1: pin names not known; wires that end beside it: S1
  Button u_K3 (.out(K3));
  Button u_K2 (.out(K2));
  Button u_K1 (.out(K1));
  Button u_K0 (.out(K0));
  contador_8bits Contador___8_bits (
    .data(out_1), .jump(JMP), .clock(S9), .reset(CLR), .out_5({L7, L6, L5, L4, L3, L2, L1, L0}));
  not not_1 (not_1_out, S0);
  not not_2 (not_2_out, S9);
  and and_1 (and_1_out, not_2_out, not_1_out);
  ROM ROM (.busAddr8({L7, L6, L5, L4, L3, L2, L1, L0}), .CLK(and_1_out), .busData16({HEX5, HEX4, HEX3, HEX2}));
  unidade_controle Controle (
    .in_1({HEX5, HEX4, HEX3, HEX2}), .clock(S9), .clear_in(S0), .r1(HEX1), .r2(HEX0), .operando(OPERANDO),
    .clock_r2(CLK_R2), .clock_r1(CLK_R1), .ula_in_b(ULA_IN_A), .ula_in_a(ULA_IN_B), .op_ula(OP_ULA),
    .jump_address(out_1), .jump(JMP), .clear(CLR), .clear_registrador(CLR_REG));

  // Other names for the same wires on the sheet: JMP_ADR[3:0] = out_1

  // Notes on the sheet:
  //   Clock S9 - Clear S0 - Memória HEX5-HEX2 - Contador L0-L7
endmodule

module ROM (
  input  CLK,
  input  [7:0] busAddr8,
  output [15:0] busData16
);

  wire [15:0] ROM_CPU_data;

  Register #(.width(16), .Select("low")) Reg16 (.D(ROM_CPU_data), .Q(busData16), .clk(CLK));  // open: en, clr
  ROM_part #(.dataWidth(16), .Select("low")) ROM_CPU (.addr(busAddr8), .data(ROM_CPU_data));

  // Notes on the sheet:
  //   contents of ROM_CPU (hex, n*v repeats v):
  //   6005 9101 6202 6304 c08 0 0 0 400 6001 9001 9002 6302 6102 9302 6200 6001 800
endmodule

module unidade_controle (
  input  [15:0] in_1,
  input  [3:0] r1,
  input  [3:0] r2,
  input  clock,
  input  clear_in,
  output [3:0] jump_address,
  output jump,
  output clear,
  output clear_registrador,
  output [1:0] op_ula,
  output clock_r2,
  output clock_r1,
  output [3:0] operando,
  output [3:0] ula_in_a,
  output [3:0] ula_in_b
);

  wire and_1_out, and_4_out, and_5_out, and_7_out, ENB_R1, ENB_R2, ENB_ULA, not_1_out, not_2_out, not_3_out,
       not_4_out, not_5_out, not_6_out, not_7_out, not_8_out, not_9_out, not_10_out;
  wire [0:0] and_9_out;

  not not_1 (not_1_out, in_1[13]);
  not not_2 (not_2_out, in_1[14]);
  not not_3 (not_3_out, in_1[10]);
  not not_4 (not_4_out, in_1[11]);
  not not_5 (not_5_out, in_1[10]);
  not not_6 (not_6_out, in_1[11]);
  not not_7 (not_7_out, in_1[12]);
  not not_8 (not_8_out, in_1[15]);
  and and_1 (and_1_out, in_1[12], not_1_out, not_2_out, in_1[15]);
  and and_2 (clock_r2, and_1_out, ENB_ULA, clock);
  and and_3 (jump, in_1[10], in_1[11]);
  and and_4 (and_4_out, not_3_out, in_1[11]);
  and and_5 (and_5_out, in_1[10], not_4_out);
  and and_6 (ENB_ULA, not_5_out, not_6_out);
  and and_7 (and_7_out, not_7_out, in_1[13], in_1[14], not_8_out);
  not not_9 (not_9_out, in_1[8]);
  not not_10 (not_10_out, ENB_R1);
  or or_1 (clear, and_4_out, clear_in);
  or or_2 (clear_registrador, clear_in, and_5_out);
  and and_8 (clock_r1, clock, ENB_ULA, and_7_out);
  not not_11 (ENB_R2, and_1_out);
  not not_12 (ENB_R1, and_7_out);
  Multiplexer #(.select(2), .width(4), .enable("false")) multiplexer_1 (
    .in0(r1), .in1(r2), .in2(in_1[3:0]), .out(ula_in_a), .sel({in_1[8], and_9_out[0]}));  // open: in3
  and and_9 (and_9_out[0], not_9_out, not_10_out, ENB_R2);

  assign jump_address = in_1[3:0];
  assign op_ula = in_1[9:8];
  assign operando = in_1[3:0];
  assign ula_in_b = in_1[3:0];

  // Other names for the same wires on the sheet: memmory_data[15:0] = in_1
endmodule
