// Logisim project registrador.circ as structural Verilog: 1 circuit, main circuit main
module main (
  input  clock,
  input  d0,
  input  d1,
  input  d2,
  input  d3,
  output q0,
  output q1,
  output q2,
  output q3
);

  wire d_ff_2_qn;

  D_Flip_Flop #(.Pre_Clr_Positions("LEGACY")) d_ff_1 (.clk(clock), .D(d0), .Q(q0));  // open: Qn, preset, reset
  D_Flip_Flop d_ff_2 (.clk(clock), .D(d1), .Q(q1), .Qn(d_ff_2_qn));  // open: preset, reset
  D_Flip_Flop d_ff_3 (.clk(clock), .D(d2), .Q(q2));  // open: Qn, preset, reset
  D_Flip_Flop d_ff_4 (.clk(clock), .D(d3), .Q(q3));  // open: Qn, preset, reset
endmodule
